// Logisim project Adder&Substracter.circ as structural Verilog: 3 circuits, main circuit main
module main (
  input  A2,
  input  A1,
  input  A0,
  input  in_4,
  input  B2,
  input  B1,
  input  B0
);

  wire and_1_out, full_adder_2_c, full_adder_2_s, full_adder_3_c, full_adder_3_s, full_adder_4_c,
       full_adder_4_s, full_adder_c, full_adder_s, half_adder_2_carry, half_adder_2_sum, half_adder_3_carry,
       half_adder_3_sum, half_adder_4_carry, half_adder_5_carry, half_adder_carry, half_adder_sum, or_1_out,
       xor_1_out, xor_2_out, xor_3_out, xor_4_out, xor_5_out, xor_6_out, xor_7_out, xor_8_out, xor_9_out,
       xor_10_out, xor_11_out;
  wire [2:0] half_adder_4_sum;

  or or_1 (or_1_out, A1, A0);
  and and_1 (and_1_out, or_1_out, A2);
  xor xor_1 (xor_1_out, A0, and_1_out);
  xor xor_2 (xor_2_out, A1, and_1_out);
  xor xor_3 (xor_3_out, 1'b0, and_1_out);
  half_adder half_adder (.y(xor_1_out), .x(and_1_out), .carry(half_adder_carry), .sum(half_adder_sum));
  half_adder half_adder_2 (.y(xor_2_out), .x(half_adder_carry), .carry(half_adder_2_carry), .sum(half_adder_2_sum));
  half_adder half_adder_3 (.y(xor_3_out), .x(half_adder_2_carry), .carry(half_adder_3_carry), .sum(half_adder_3_sum));
  Hex_Digit_Display hex_digit_display_1 (.value({1'b0, half_adder_4_sum}));  // open: dp
  LED led_1 (.in(full_adder_4_s));
  xor xor_4 (xor_4_out, B0, xor_8_out);
  xor xor_5 (xor_5_out, B1, xor_8_out);
  xor xor_6 (xor_6_out, 1'b0, xor_8_out);
  xor xor_7 (xor_7_out, 1'b0, xor_8_out);
  xor xor_8 (xor_8_out, B2, in_4);
  full_adder full_adder (
    .previous_carry(xor_8_out), .x(half_adder_sum), .y(xor_4_out), .s(full_adder_s), .c(full_adder_c));
  full_adder full_adder_2 (
    .previous_carry(full_adder_c), .x(half_adder_2_sum), .y(xor_5_out), .s(full_adder_2_s), .c(full_adder_2_c));
  full_adder full_adder_3 (
    .previous_carry(full_adder_2_c), .x(xor_6_out), .y(half_adder_3_sum), .s(full_adder_3_s),
    .c(full_adder_3_c));
  full_adder full_adder_4 (
    .previous_carry(full_adder_3_c), .x(and_1_out), .y(xor_7_out), .s(full_adder_4_s), .c(full_adder_4_c));
  xor xor_9 (xor_9_out, full_adder_4_s, full_adder_s);
  xor xor_10 (xor_10_out, full_adder_2_s, full_adder_4_s);
  xor xor_11 (xor_11_out, full_adder_3_s, full_adder_4_s);
  half_adder half_adder_4 (.y(xor_9_out), .x(full_adder_4_s), .carry(half_adder_4_carry), .sum(half_adder_4_sum[0]));
  half_adder half_adder_5 (
    .y(xor_10_out), .x(half_adder_4_carry), .carry(half_adder_5_carry), .sum(half_adder_4_sum[1]));
  half_adder half_adder_6 (.y(xor_11_out), .x(half_adder_5_carry), .sum(half_adder_4_sum[2]));  // open: carry
  // also tied to GND on the sheet: {half_adder_3_carry, full_adder_4_c}
endmodule

module full_adder (
  input  previous_carry,
  input  x,
  input  y,
  output s,
  output c
);

  wire and_1_out, and_2_out, xor_1_out;

  xor xor_1 (xor_1_out, x, y);
  and and_1 (and_1_out, x, y);
  xor xor_2 (s, xor_1_out, previous_carry);
  and and_2 (and_2_out, xor_1_out, previous_carry);
  or or_1 (c, and_2_out, and_1_out);
endmodule

module half_adder (
  input  x,
  input  y,
  output sum,
  output carry
);

  xor xor_1 (sum, x, y);
  and and_1 (carry, x, y);
endmodule
