// Logisim project Full_project_V3.circ as structural Verilog: 14 circuits, main circuit full circuit v3
module full_circuit_v3 (
  input  B2,
  input  B1,
  input  B0,
  input  A2,
  input  A1,
  input  A0,
  input  _1_0__x,
  input  in_8
);

  wire Adder_and_subtractor_circuit_out_8, Adder_and_subtractor_circuit_out_9,
       Adder_and_subtractor_circuit_out_10, Adder_and_subtractor_circuit_out_11, and_1_out, and_2_out,
       and_3_out, and_4_out, and_5_out, and_6_out, and_7_out, and_8_out, and_9_out, and_10_out, and_11_out,
       multiplexer_1_out, multiplexer_2_out, multiplexer_3_out, multiplexer_4_out, multiplexer_5_out,
       multiplier_circuit_out_7, multiplier_circuit_out_8, multiplier_circuit_out_9,
       multiplier_circuit_out_10, multiplier_circuit_out_11, n7447_1_out_5, n7447_1_out_6, n7447_1_out_7,
       n7447_1_out_8, n7447_1_out_9, n7447_1_out_10, n7447_1_out_11, not_1_out, not_2_out, not_3_out,
       or_1_out, or_2_out, or_3_out, reminder_1_r0, reminder_1_r1, reminder_1_sign, reminder_1_zeroflage;

  adder_and_subtractor Adder_and_subtractor_circuit (
    .in_1(in_8), .A2(A2), .A1(A1), .A0(A0), .out_8(Adder_and_subtractor_circuit_out_8),
    .out_9(Adder_and_subtractor_circuit_out_9), .out_10(Adder_and_subtractor_circuit_out_10),
    .out_11(Adder_and_subtractor_circuit_out_11), .B2(B2), .B1(B1), .B0(B0));
  multipier_ic multiplier_circuit (
    .A0(A0), .A1(A1), .A2(A2), .B0(B0), .B1(B1), .B2(B2), .out_7(multiplier_circuit_out_7),
    .out_8(multiplier_circuit_out_8), .out_9(multiplier_circuit_out_9), .out_10(multiplier_circuit_out_10),
    .out_11(multiplier_circuit_out_11));
  reminder reminder_1 (
    .A0(A0), .A1(A1), .A2(A2), .B0(B0), .B1(B1), .r0(reminder_1_r0), .r1(reminder_1_r1),
    .sign(reminder_1_sign), .zeroflage(reminder_1_zeroflage));  // open: B2
  Multiplexer #(.select(2), .enable("false")) multiplexer_1 (
    .in0(Adder_and_subtractor_circuit_out_11), .in1(Adder_and_subtractor_circuit_out_11),
    .in2(multiplier_circuit_out_11), .in3(reminder_1_sign), .out(multiplexer_1_out), .sel({_1_0__x, in_8}));
  Multiplexer #(.select(2), .enable("false")) multiplexer_2 (
    .in0(Adder_and_subtractor_circuit_out_8), .in1(Adder_and_subtractor_circuit_out_8),
    .in2(multiplier_circuit_out_7), .in3(reminder_1_r0), .out(multiplexer_2_out), .sel({_1_0__x, in_8}));
  Multiplexer #(.select(2), .enable("false")) multiplexer_3 (
    .in0(Adder_and_subtractor_circuit_out_9), .in1(Adder_and_subtractor_circuit_out_9),
    .in2(multiplier_circuit_out_8), .in3(reminder_1_r1), .out(multiplexer_3_out), .sel({_1_0__x, in_8}));
  Multiplexer #(.select(2), .enable("false")) multiplexer_4 (
    .in0(Adder_and_subtractor_circuit_out_10), .in1(Adder_and_subtractor_circuit_out_10),
    .in2(multiplier_circuit_out_9), .in3(1'b0), .out(multiplexer_4_out), .sel({_1_0__x, in_8}));
  Multiplexer #(.select(2), .enable("false")) multiplexer_5 (
    .in0(1'b0), .in1(1'b0), .in2(multiplier_circuit_out_10), .in3(1'b0), .out(multiplexer_5_out),
    .sel({_1_0__x, in_8}));
  and and_1 (and_1_out, in_8, _1_0__x);
  _7447 u_7447_1 (
    .A(multiplexer_2_out), .B(multiplexer_3_out), .C(multiplexer_4_out), .D(multiplexer_5_out),
    .out_5(n7447_1_out_5), .out_6(n7447_1_out_6), .out_7(n7447_1_out_7), .out_8(n7447_1_out_8),
    .out_9(n7447_1_out_9), .out_10(n7447_1_out_10), .out_11(n7447_1_out_11));
  and and_2 (and_2_out, and_1_out, reminder_1_zeroflage);
  not not_1 (not_1_out, and_2_out);
  or or_1 (or_1_out, multiplexer_2_out, multiplexer_3_out);
  or or_2 (or_2_out, or_1_out, multiplexer_4_out);
  or or_3 (or_3_out, or_2_out, multiplexer_5_out);
  LED led_1 (.in(and_2_out));
  and and_3 (and_3_out, n7447_1_out_5, not_1_out);
  and and_4 (and_4_out, n7447_1_out_6, not_1_out);
  and and_5 (and_5_out, n7447_1_out_7, not_1_out);
  not not_2 (not_2_out, and_10_out);
  and and_6 (and_6_out, n7447_1_out_8, not_1_out);
  and and_7 (and_7_out, n7447_1_out_9, not_1_out);
  and and_8 (and_8_out, n7447_1_out_10, not_1_out);
  and and_9 (and_9_out, n7447_1_out_11, not_1_out);
  and and_10 (and_10_out, not_1_out, not_3_out);
  not not_3 (not_3_out, or_3_out);
  and and_11 (and_11_out, multiplexer_1_out, not_2_out);
  _7_Segment_Display u_7_segment_display_1 (.g(and_11_out));  // open: f, a, b, e, d, c, dp
  _7_Segment_Display u_7_segment_display_2 (
    .g(and_6_out), .f(and_5_out), .a(and_4_out), .b(and_3_out), .e(and_9_out), .d(and_8_out), .c(and_7_out));  // open: dp
  LED led_2 (.in(and_10_out));

  // Notes on the sheet:
  //   0&0 = +
  //   0&1= -
  //   1&1=%
  //   divide by zero flag
  //   zero flag
endmodule

module Half_adder (
  input  x,
  input  y,
  output s,
  output c
);

  xor xor_1 (s, x, y);
  and and_1 (c, x, y);
endmodule

module full_adder (
  input  x,
  input  y,
  input  cin,
  output out_4,
  output out_5
);

  wire half_adder_1_c, half_adder_1_s, half_adder_2_c;

  Half_adder half_adder_1 (.x(x), .y(y), .s(half_adder_1_s), .c(half_adder_1_c));
  Half_adder half_adder_2 (.x(half_adder_1_s), .y(cin), .s(out_4), .c(half_adder_2_c));
  or or_1 (out_5, half_adder_2_c, half_adder_1_c);

  // Notes on the sheet:
  //   s
  //   cout
endmodule

module _4_bit_adder (
  input  Cin,
  input  a0,
  input  a1,
  input  a2,
  input  a3,
  input  b0,
  input  b2,
  input  b3,
  input  b4,
  output s0,
  output s1,
  output s2,
  output s3,
  output Cout
);

  wire full_adder_1_out_5, full_adder_2_out_5, full_adder_3_out_5;

  full_adder full_adder_1 (.x(a0), .y(b0), .cin(Cin), .out_4(s0), .out_5(full_adder_1_out_5));
  full_adder full_adder_2 (.x(a1), .y(b2), .cin(full_adder_1_out_5), .out_4(s1), .out_5(full_adder_2_out_5));
  full_adder full_adder_3 (.x(a2), .y(b3), .cin(full_adder_2_out_5), .out_4(s2), .out_5(full_adder_3_out_5));
  full_adder full_adder_4 (.x(a3), .y(b4), .cin(full_adder_3_out_5), .out_4(s3), .out_5(Cout));
endmodule

// XOR
module Xor_ic (
  input  in_1,
  input  in_2,
  input  in_3,
  input  in_4,
  input  in_5,
  input  in_6,
  input  in_7,
  input  in_8,
  output out_9,
  output out_10,
  output out_11,
  output out_12
);

  xor xor_1 (out_9, in_1, in_2);
  xor xor_2 (out_10, in_3, in_4);
  xor xor_3 (out_11, in_5, in_6);
  xor xor_4 (out_12, in_7, in_8);
endmodule

module _7447 (
  input  A,
  input  B,
  input  C,
  input  D,
  output out_5,
  output out_6,
  output out_7,
  output out_8,
  output out_9,
  output out_10,
  output out_11
);

  wire and_1_out, and_2_out, and_3_out, and_4_out, and_5_out, and_6_out, and_7_out, and_8_out, and_9_out,
       not_1_out, not_2_out, not_3_out;

  not not_1 (not_1_out, C);
  not not_2 (not_2_out, B);
  not not_3 (not_3_out, A);
  and and_1 (and_1_out, not_1_out, not_3_out);
  and and_2 (and_2_out, C, A);
  and and_3 (and_3_out, C, not_3_out);
  and and_4 (and_4_out, B, A);
  and and_5 (and_5_out, not_2_out, not_3_out);
  and and_6 (and_6_out, B, not_3_out);
  and and_7 (and_7_out, C, A, not_2_out);
  and and_8 (and_8_out, not_1_out, B);
  and and_9 (and_9_out, C, not_2_out);
  or or_1 (out_7, D, and_5_out, and_9_out, and_3_out);
  or or_2 (out_8, D, and_6_out, and_8_out, and_9_out);
  or or_3 (out_6, D, B, and_1_out, and_2_out);
  or or_4 (out_5, D, not_1_out, and_4_out, and_5_out);
  or or_5 (out_9, C, and_5_out, A);
  or or_6 (out_10, D, and_1_out, and_8_out, and_7_out, and_6_out);
  or or_7 (out_11, and_1_out, and_6_out);
endmodule

module multiplier (
  input  A0,
  input  A1,
  input  B0,
  input  B1,
  input  A2,
  input  B2,
  output out_7,
  output out_8,
  output out_9,
  output out_10,
  output out_11
);

  wire and_2_out, and_3_out, and_4_out, and_5_out;

  and and_1 (out_7, A0, B0);
  and and_2 (and_2_out, A1, B0);
  and and_3 (and_3_out, A0, B1);
  and and_4 (and_4_out, A1, B1);
  and and_5 (and_5_out, and_2_out, and_3_out);
  xor xor_1 (out_11, A2, B2);
  xor xor_2 (out_8, and_2_out, and_3_out);
  and and_6 (out_10, and_5_out, and_4_out);
  xor xor_3 (out_9, and_5_out, and_4_out);
endmodule

// AND
module And_ic (
  input  in_1,
  input  in_2,
  input  in_3,
  input  in_4,
  input  in_5,
  input  in_6,
  input  in_7,
  input  in_8,
  output out_9,
  output out_10,
  output out_11,
  output out_12
);

  and and_1 (out_9, in_1, in_2);
  and and_2 (out_10, in_3, in_4);
  and and_3 (out_11, in_5, in_6);
  and and_4 (out_12, in_7, in_8);
endmodule

module Not (
  input  in_1,
  input  in_2,
  input  in_3,
  input  in_4,
  input  in_5,
  input  in_6,
  output out_7,
  output out_8,
  output out_9,
  output out_10,
  output out_11,
  output out_12
);

  not not_1 (out_7, in_1);
  not not_2 (out_8, in_2);
  not not_3 (out_9, in_3);
  not not_4 (out_10, in_4);
  not not_5 (out_11, in_5);
  not not_6 (out_12, in_6);
endmodule

module multipier_ic (
  input  A0,
  input  A1,
  input  A2,
  input  B0,
  input  B1,
  input  B2,
  output out_7,
  output out_8,
  output out_9,
  output out_10,
  output out_11
);

  wire and_1_out, and_ic_1_out_10, and_ic_1_out_11, and_ic_1_out_12;

  And_ic and_ic_1 (
    .in_1(A0), .in_2(B0), .in_3(A1), .in_4(B0), .in_5(A0), .in_6(B1), .in_7(A1), .in_8(B1), .out_9(out_7),
    .out_10(and_ic_1_out_10), .out_11(and_ic_1_out_11), .out_12(and_ic_1_out_12));
  and and_1 (and_1_out, and_ic_1_out_10, and_ic_1_out_11);
  Xor_ic xor_ic_1 (
    .in_1(and_ic_1_out_10), .in_2(and_ic_1_out_11), .in_3(and_1_out), .in_4(and_ic_1_out_12), .in_5(A2),
    .in_6(B2), .out_9(out_8), .out_10(out_9), .out_11(out_11));  // open: in_7, in_8, out_12
  and and_2 (out_10, and_1_out, and_ic_1_out_12);
endmodule

// Reminder
module reminder (
  input  A0,
  input  A1,
  input  A2,
  input  B0,
  input  B1,
  input  B2,
  output r0,
  output r1,
  output sign,
  output zeroflage
);

  wire and_1_out, and_2_out, and_ic_1_out_9, and_ic_1_out_10, and_ic_1_out_11, and_ic_1_out_12,
       and_ic_2_out_9, and_ic_2_out_10, and_ic_2_out_11, comparator_1_gt, comparator_1_lt, nor_2_out,
       not_1_out, not_2_out, not_3_out, or_1_out, or_2_out, or_3_out;

  Comparator #(.width(2), .mode("unsigned")) comparator_1 (
    .a({A1, A0}), .b({B1, B0}), .gt(comparator_1_gt), .lt(comparator_1_lt));  // open: eq
  nor nor_1 (zeroflage, B0, B1);
  And_ic and_ic_1 (
    .in_1(comparator_1_gt), .in_2(A0), .in_3(A1), .in_4(comparator_1_gt), .in_5(B0), .in_6(comparator_1_gt),
    .in_7(B1), .in_8(comparator_1_gt), .out_9(and_ic_1_out_9), .out_10(and_ic_1_out_10),
    .out_11(and_ic_1_out_11), .out_12(and_ic_1_out_12));
  not not_1 (not_1_out, and_ic_1_out_11);
  And_ic and_ic_2 (
    .in_1(and_ic_1_out_9), .in_2(and_ic_1_out_10), .in_3(not_1_out), .in_4(and_ic_1_out_12),
    .in_5(and_ic_2_out_9), .in_6(and_ic_2_out_10), .out_9(and_ic_2_out_9), .out_10(and_ic_2_out_10),
    .out_11(and_ic_2_out_11));  // open: in_7, in_8, out_12
  and and_1 (and_1_out, comparator_1_lt, A0);
  and and_2 (and_2_out, comparator_1_lt, A1);
  or or_1 (or_1_out, and_ic_2_out_11, and_1_out);
  or or_2 (or_2_out, 1'b0, and_2_out);
  not not_2 (not_2_out, zeroflage);
  and and_3 (r0, or_1_out, not_2_out);
  and and_4 (r1, or_2_out, not_2_out);
  or or_3 (or_3_out, nor_2_out, zeroflage);
  nor nor_2 (nor_2_out, r0, r1);
  and and_5 (sign, A2, not_3_out);
  not not_3 (not_3_out, or_3_out);
endmodule

module adder_and_subtractor (
  input  in_1,
  input  A2,
  input  A1,
  input  A0,
  input  B2,
  input  B1,
  input  B0,
  output out_8,
  output out_9,
  output out_10,
  output out_11
);

  wire and_1_out, full_adder_2_c, full_adder_2_s, full_adder_3_c, full_adder_3_s, full_adder_4_c,
       full_adder_c, full_adder_s, half_adder_2_carry, half_adder_2_sum, half_adder_3_carry,
       half_adder_3_sum, half_adder_4_carry, half_adder_5_carry, half_adder_carry, half_adder_sum, or_1_out,
       xor_1_out, xor_2_out, xor_3_out, xor_4_out, xor_5_out, xor_6_out, xor_7_out, xor_8_out, xor_9_out,
       xor_10_out, xor_11_out;

  or or_1 (or_1_out, A1, A0);
  and and_1 (and_1_out, or_1_out, A2);
  xor xor_1 (xor_1_out, A0, and_1_out);
  xor xor_2 (xor_2_out, A1, and_1_out);
  xor xor_3 (xor_3_out, 1'b0, and_1_out);
  half_add half_adder (.y(xor_1_out), .x(and_1_out), .carry(half_adder_carry), .sum(half_adder_sum));
  half_add half_adder_2 (.y(xor_2_out), .x(half_adder_carry), .carry(half_adder_2_carry), .sum(half_adder_2_sum));
  half_add half_adder_3 (.y(xor_3_out), .x(half_adder_2_carry), .carry(half_adder_3_carry), .sum(half_adder_3_sum));
  xor xor_4 (xor_4_out, B0, xor_8_out);
  xor xor_5 (xor_5_out, B1, xor_8_out);
  xor xor_6 (xor_6_out, 1'b0, xor_8_out);
  xor xor_7 (xor_7_out, 1'b0, xor_8_out);
  xor xor_8 (xor_8_out, B2, in_1);
  full_add full_adder (
    .previous_carry(xor_8_out), .x(half_adder_sum), .y(xor_4_out), .s(full_adder_s), .c(full_adder_c));
  full_add full_adder_2 (
    .previous_carry(full_adder_c), .x(half_adder_2_sum), .y(xor_5_out), .s(full_adder_2_s), .c(full_adder_2_c));
  full_add full_adder_3 (
    .previous_carry(full_adder_2_c), .x(xor_6_out), .y(half_adder_3_sum), .s(full_adder_3_s),
    .c(full_adder_3_c));
  full_add full_adder_4 (.previous_carry(full_adder_3_c), .x(and_1_out), .y(xor_7_out), .s(out_11), .c(full_adder_4_c));
  xor xor_9 (xor_9_out, out_11, full_adder_s);
  xor xor_10 (xor_10_out, full_adder_2_s, out_11);
  xor xor_11 (xor_11_out, full_adder_3_s, out_11);
  half_add half_adder_4 (.y(xor_9_out), .x(out_11), .carry(half_adder_4_carry), .sum(out_8));
  half_add half_adder_5 (.y(xor_10_out), .x(half_adder_4_carry), .carry(half_adder_5_carry), .sum(out_9));
  half_add half_adder_6 (.y(xor_11_out), .x(half_adder_5_carry), .sum(out_10));  // open: carry
  // also tied to GND on the sheet: {half_adder_3_carry, full_adder_4_c}
endmodule

module full_add (
  input  previous_carry,
  input  x,
  input  y,
  output s,
  output c
);

  wire and_1_out, and_2_out, xor_1_out;

  xor xor_1 (xor_1_out, x, y);
  and and_1 (and_1_out, x, y);
  xor xor_2 (s, xor_1_out, previous_carry);
  and and_2 (and_2_out, xor_1_out, previous_carry);
  or or_1 (c, and_2_out, and_1_out);
endmodule

module half_add (
  input  x,
  input  y,
  output sum,
  output carry
);

  xor xor_1 (sum, x, y);
  and and_1 (carry, x, y);
endmodule
