// Logisim project Multiplier.circ as structural Verilog: 1 circuit, main circuit main
module main (
  input  A0,
  input  A1,
  input  B0,
  input  B1,
  input  A2,
  input  B2,
  output out_7,
  output out_8,
  output out_9,
  output out_10,
  output out_11
);

  wire and_2_out, and_3_out, and_4_out, and_5_out;

  and and_1 (out_7, A0, B0);
  and and_2 (and_2_out, A1, B0);
  and and_3 (and_3_out, A0, B1);
  and and_4 (and_4_out, A1, B1);
  and and_5 (and_5_out, and_2_out, and_3_out);
  xor xor_1 (out_11, A2, B2);
  xor xor_2 (out_8, and_2_out, and_3_out);
  and and_6 (out_10, and_5_out, and_4_out);
  xor xor_3 (out_9, and_5_out, and_4_out);
endmodule
