// Logisim project remainder (1).circ as structural Verilog: 2 circuits, main circuit main
module main (
  input  in_1,
  input  in_2,
  input  in_3,
  input  in_4,
  input  in_5,
  input  in_6,
  output out_7
);

  wire and_1_out, and_2_out, and_3_out, and_4_out, and_5_out, and_6_out, comparator_1_gt, comparator_1_lt,
       nor_1_out, nor_2_out, not_1_out, not_2_out, or_1_out, or_2_out, or_3_out, part_1_out_5, part_1_out_6;
  wire [1:0] and_7_out;

  Comparator #(.width(2), .mode("unsigned")) comparator_1 (
    .a({in_2, in_1}), .b({in_5, in_4}), .gt(comparator_1_gt), .lt(comparator_1_lt));  // open: eq
  nor nor_1 (nor_1_out, in_4, in_5);
  and and_1 (and_1_out, comparator_1_gt, in_1);
  and and_2 (and_2_out, comparator_1_gt, in_2);
  and and_3 (and_3_out, comparator_1_gt, in_4);
  and and_4 (and_4_out, comparator_1_gt, in_5);
  circuit part_1 (
    .in_1(and_1_out), .in_2(and_2_out), .in_3(and_3_out), .in_4(and_4_out), .out_5(part_1_out_5),
    .out_6(part_1_out_6));
  and and_5 (and_5_out, comparator_1_lt, in_1);
  and and_6 (and_6_out, comparator_1_lt, in_2);
  or or_1 (or_1_out, part_1_out_5, and_5_out);
  or or_2 (or_2_out, part_1_out_6, and_6_out);
  not not_1 (not_1_out, nor_1_out);
  and and_7 (and_7_out[0], or_1_out, not_1_out);
  and and_8 (and_7_out[1], or_2_out, not_1_out);
  or or_3 (or_3_out, nor_2_out, nor_1_out);
  nor nor_2 (nor_2_out, and_7_out[0], and_7_out[1]);
  LED led_1 (.in(nor_1_out));
  and and_9 (out_7, in_3, not_2_out);
  not not_2 (not_2_out, or_3_out);
  Hex_Digit_Display hex_digit_display_1 (.value({2'b00, and_7_out}));  // open: dp
endmodule

module circuit (
  input  in_1,
  input  in_2,
  input  in_3,
  input  in_4,
  output out_5,
  output out_6
);

  wire not_1_out;

  not not_1 (not_1_out, in_3);
  and and_1 (out_5, in_1, in_2, in_4, not_1_out);

  assign out_6 = 1'b0;
endmodule
